# Fritzing sketch Lily Car - Wiring Diagram-2 (saved by Fritzing 0.9.4)
breadboards: 2

parts:
  L298N1 = L298N DC motor driver
  VCC1 = Battery
  Raspberry_Pi_1 = Raspberry Pi 3 [part_number=RPI-3-V1.2]
  Part2 = Photon
  Meadow1 = Meadow F7 Micro  # not connected
  VCC2 = Battery  # not connected
  Reg1 = DC-DC CONVERTER [part_number=80633 package=dc-dc_converter]
  Reg2 = DC-DC CONVERTER [part_number=80633 package=dc-dc_converter]  # not connected
  Reg3 = DC-DC CONVERTER [part_number=80633 package=dc-dc_converter]  # not connected
  VCC3 = Battery block 9V
  U1 = 74HC595 [package="DIP16 [THT]"]

nets:
  N1: L298N1.5VEN#8, Raspberry_Pi_1.GPIO23
  N2: L298N1.5V#9, Raspberry_Pi_1.GPIO25
  N3: L298N1.5V#10, Raspberry_Pi_1.GPIO24
  N4: L298N1.ENA, L298N1.ENB, L298N1.IN1, L298N1.5VEN#17, Raspberry_Pi_1.GPIO12, U1.Q3
  N5: L298N1.IN2, U1.Q2
  N6: L298N1.IN3, U1.Q1
  N7: L298N1.IN4, U1.Q0
  N8: VCC1.-, Reg1.IN-
  N9: VCC1.+, Reg1.IN+
  N10: Raspberry_Pi_1.GPIO11, U1.SH_CP
  GND: Raspberry_Pi_1.GND, VCC3.-, U1.Q5, U1.Q6, U1.Q7, U1.GND
  N11: Raspberry_Pi_1.GPIO21, U1.ST_CP
  N12: Raspberry_Pi_1.GPIO20, U1.DS
  N13: Raspberry_Pi_1.GPIO16, U1.OE
  5V: Raspberry_Pi_1.5V, VCC3.+, U1.VCC
  N14: Part2.GND, Reg1.OUT-
  N15: Part2.3V3, Reg1.OUT+

custom parts:
  L298N DC motor driver: 2x DC motor driver with 78M05 positive voltage regulator (7..35 V) L298N: max 46 V, 2 A Set 5 V Enable jumper to enable 5 V regultor (needed for the L298N) and +5 V output at screw terminal or supply external +5 V at screw terminal Set ENA and/or ENB to +5 V to enable motor permanently or supply ENA and/or ENB with PWM signal IN1 and IN2 set rotation directory for motor A (OUT1/OUT2) IN2 and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
  Meadow F7 Micro: A prototyping board running full .Net Standard 2.X
  DC-DC CONVERTER: WYHP 5A constant current/voltage manufactured by Shenzhen Weiyapuhua Technology Co., Ltd
